# Fritzing sketch UmbrellaStand_Breadboard (saved by Fritzing 0.9.3b)
stripboards: 1

parts:
  U1 = ESP8266 WiFi Module [part_number=ESP8266]
  sad = BLE Mini
  TFT1 = Adafruit 2.8" TFT
  Part2 = Arduino Due (Rev2b)
  J1 = Piezo Speaker
  S1 = Pushbutton [package="[THT]"]
  S2 = Pushbutton [package="[THT]"]
  S3 = Pushbutton [package="[THT]"]
  PIR1 = PIR sensor
  S4 = Pushbutton [package="[THT]"]
  S5 = Pushbutton [package="[THT]"]

nets (from the breadboard view):
  N1: U1.RXD, Part2.D14/TX3
  VIN: U1.VCC, sad.VIN, TFT1.Vin, Part2.3V3
  GND: U1.GND, sad.GND, TFT1.GND, Part2.GND, J1.pin1, S1.Pin_1, S1.Pin_2, S2.Pin_1, S2.Pin_2, S3.Pin_1, S3.Pin_2, PIR1.GND, S4.Pin_1, S4.Pin_2, S5.Pin_1, S5.Pin_2
  N2: U1.TXD, Part2.D15/RX3
  N3: sad.RX, Part2.D18/TX1
  N4: sad.TX, Part2.D19/RX1
  N5: TFT1.CLK, Part2.SCK
  N6: TFT1.MISO, Part2.MISO
  N7: TFT1.MOSI, Part2.MOSI
  N8: TFT1.CS, Part2.D2_PWM
  N9: TFT1.D/C, Part2.D3_PWM
  N10: TFT1.Lite, Part2.D4_PWM/SS1
  N11: TFT1.CCS, Part2.D5_PWM
  5V: Part2.5V, PIR1.VDD
  N12: Part2.D13_PWM, J1.pin2
  N13: Part2.D31, S1.Pin_3, S1.Pin_4
  N14: Part2.D33, S2.Pin_4
  N15: Part2.D35, S3.Pin_4
  N16: Part2.D39, PIR1.SIG
  N17: Part2.D45, S4.Pin_3
  N18: Part2.D47, S5.Pin_3, S5.Pin_4

notes:
  Front Buttons
  Hooks

custom parts:
  ESP8266 WiFi Module: Generic WiFi Module based on the ESP8266 with onboard PCB antenna and UART communications
  BLE Mini: RedBear BLE Mini
  Adafruit 2.8" TFT: Adafruit 2.8" TFT lcd screen
  Arduino Due (Rev2b): The Arduino Due is a microcontroller board based on the Atmel SAM3X8E ARM Cortex-M3 CPU (datasheet). It is the first Arduino board based on a 32-bit ARM core microcontroller. It has 54 digital input/output pins (of which 12 can be used as PWM outputs), 12 analog inputs, 4 UARTs (hardware serial ports), a 84 MHz clock, an USB OTG capable connection, 2 DAC (digital to analog), 2 TWI, a power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
